# Fritzing sketch scematics (saved by Fritzing 0.9.3b)

parts:
  Part1 = Arduino Nano (Rev3.0) (ICSP)
  ZS-042_RTC1 = ZS-042 RTC Module
  BT1 = Bluetooth HC-06u [package=THT]
  U1 = WS2812 RGB LED strip
  U3 = LIPO-2000mAh [package=lipo-2000]
  U4 = LIPO-2000mAh [package=lipo-2000]  # not connected
  TP1 = TP4056 [chip_label=TP4056 package="DIP (Dual Inline) [THT]"]
  U5 = Mini-360 DC-DC Buck converter [package=THT]

nets:
  N1: Part1.D1/TX, BT1.RXD
  N2: Part1.D0/RX, BT1.TXD
  N3: Part1.D3, U1.DIN
  VIN: Part1.VIN, ZS-042_RTC1.VCC, U5.OUT+
  GND: Part1.GND, ZS-042_RTC1.GND, BT1.GND, U5.OUT-
  N4: Part1.A5, ZS-042_RTC1.SCL
  N5: Part1.A4, ZS-042_RTC1.SDA
  N6: U3.+, TP1.pin4
  N7: U3.-, TP1.pin5
  N8: TP1.pin3, U5.IN+
  N9: TP1.pin6, U5.IN-

custom parts:
  Bluetooth HC-06u: Bluetooth HC-06 - face up, pins down 16.5mm x 37.5mm PCB
  WS2812 RGB LED strip: WS2812 strip
  TP4056: A DIP stand-in part for whatever IC you want. With 6 pins on a 300mil dual inline package (DIP) footprint.
  Mini-360 DC-DC Buck converter: Mini-360 DC-DC Buck converter. Tiny buck step down voltage converter, input voltage 4.75 to 23V output 1 to 17V adjustable. Available from ebay and the like.
